// Logisim project cache2waylogisim.circ as structural Verilog
module main (
  input  [31:0] Address,
  output Hit,
  output [31:0] Data_output,
  output miss,
  output [20:0] Tag,
  output set0,
  output set1,
  output [4:0] Index,
  output [5:0] Offset
);

  wire Clk_out;

  Clock Clk (.out(Clk_out));
  cacheLRU cachelru_1 (
    .clock(Clk_out), .Address(Address), .hit(Hit), .data_out(Data_output), .tag_out(Tag), .index_out(Index),
    .offset_out(Offset), .miss_out(miss), .set_0(set0), .set_1(set1));
endmodule

// VHDL entity cache, as the project stores it:
library IEEE;
use IEEE.STD_LOGIC_1164.ALL;
use IEEE.STD_LOGIC_ARITH.ALL;
use IEEE.STD_LOGIC_UNSIGNED.ALL;

entity cache is
    Port (
        clk : in std_logic;
        reset : in std_logic;
        address : in std_logic_vector(31 downto 0);
        write_data : in std_logic_vector(31 downto 0);
        write_enable : in std_logic;
        read_data : out std_logic_vector(31 downto 0);
        hit : out std_logic
    );
end cache;

architecture Behavioral of cache is
    -- Cache parameters
    constant CACHE_SIZE : integer := 256;  -- Number of sets
    constant ASSOCIATIVITY : integer := 2; -- 2-way associative

    -- Type declarations
    type cache_line is record
        valid : std_logic;
        tag : std_logic_vector(23 downto 0);
        data : std_logic_vector(31 downto 0);
    end record;

    type cache_set is array (0 to ASSOCIATIVITY-1) of cache_line;
    type cache_array is array (0 to CACHE_SIZE-1) of cache_set;

    -- Cache memory
    signal cache : cache_array := (others => (others => (valid => '0', tag => (others => '0'), data => (others => '0'))));

    -- Internal signals
    signal index : integer range 0 to CACHE_SIZE-1;
    signal tag : std_logic_vector(23 downto 0);
    signal offset : std_logic_vector(1 downto 0);
    signal hit_way : integer range 0 to ASSOCIATIVITY-1;
    signal found : std_logic;
    signal way : integer range 0 to ASSOCIATIVITY-1;

begin
    process(clk, reset)
    begin
        if reset = '1' then
            for i in 0 to CACHE_SIZE-1 loop
                for j in 0 to ASSOCIATIVITY-1 loop
                    cache(i)(j).valid <= '0';
                    cache(i)(j).tag <= (others => '0');
                    cache(i)(j).data <= (others => '0');
                end loop;
            end loop;
            read_data <= (others => '0');
            hit <= '0';

        elsif rising_edge(clk) then
            -- Extract index, tag, and offset from address
            index <= conv_integer(address(31 downto 24));   -- 8-bit index
            tag <= address(23 downto 0);			     -- 24-bit index
            offset <= address(1 downto 0);				-- 2-bit offset
            
            -- Check for cache hit
            found <= '0';
           if cache(index)(way).valid = '1' and cache(index)(way).tag = tag then
               found <= '1';
               hit_way <= way;
           end if;

            if found = '1' then
                -- Cache hit
                hit <= '1';
                read_data <= cache(index)(hit_way).data;
                if write_enable = '1' then
                    cache(index)(hit_way).data <= write_data;
                end if;
            else
                -- Cache miss
                hit <= '0';
                read_data <= (others => '0');
                -- Write operation (if enabled)
                if write_enable = '1' then
                    cache(index)(0).valid <= '1';  -- Simple policy: replace way 0
                    cache(index)(0).tag <= tag;
                    cache(index)(0).data <= write_data;
                end if;
            end if;
        end if;
    end process;
end Behavioral;

// VHDL entity classCache, as the project stores it:
--------------------------------------------------------------------------------
-- Description :
-- Cache for pipelined MIPS processor. 
-- 2 way associative.
-- 32 bit addresses and 32 bit data output. 
-- Address is divided this way: 
--  tag is of 10 bits, index is of 8 bits and offset is 5 bits. 
--------------------------------------------------------------------------------

LIBRARY ieee;
USE ieee.std_logic_1164.all;

USE ieee.numeric_std.all;  

ENTITY classCache IS
  PORT (
  ------------------------------------------------------------------------------
  --Insert input ports below
    clock      : IN  std_logic;           
    Address: IN std_logic_vector(31 DOWNTO 0);

  ------------------------------------------------------------------------------
	hit : OUT std_logic; 
	data_out: OUT std_logic_vector(31 DOWNTO 0);
		tag_out : OUT std_logic_vector (10 DOWNTO 0); 
		index_out : OUT std_logic_vector (8 DOWNTO 0); 
		offset_out :OUT std_logic_vector (5 DOWNTO 0);
	miss_out: OUT std_logic
    );
END classCache;

--------------------------------------------------------------------------------
--Complete your VHDL description below
--------------------------------------------------------------------------------

ARCHITECTURE TypeArchitecture OF classCache IS

type bloque is array(0 to 63) of std_logic_vector(10 downto 0);
type t_set is array(0 to 255) of bloque;
signal cache0 : t_set;
signal cache1 : t_set; 

type t_tag is array(0 to 255) of std_logic_vector(10 downto 0);

type t_valid is array(0 to 255) of std_logic;

type t_Dirty is array(0 to 255) of std_logic;



signal s_tag : std_logic_vector(10 downto 0);
signal s_index :std_logic_vector (8 DOWNTO 0); 
signal s_offset : std_logic_vector (5 DOWNTO 0); 

signal data: std_logic_vector(31 DOWNTO 0); 
signal hit_addr : std_logic;


type t_Memory is array (0 to 31) of std_logic_vector(31 downto 0);
signal mainmem : t_Memory:= ("00000000000000000000000000000001",others =>"00000000000000000000000000100000");

signal dirtys0 : t_Dirty;
signal valids0 : t_valid:= ('1', '0','0','0', others => '0');
signal tags0 : t_tag:=( others => "00000000000");

signal dirtys1 : t_Dirty;
signal valids1 : t_valid:= ('1', '0','0','0', others => '0');
signal tags1 : t_tag:=( others => "00000000000");

signal miss : std_logic; 

BEGIN

process (clock)
	begin
	if clock = '1' then
		s_tag <= Address(25 DOWNTO 15); 
		s_index <= Address(14  DOWNTO 6); 
		s_offset <= Address(5  DOWNTO 0); 
		hit_addr <= '0'; 
		if valids0(to_integer(unsigned(s_index))) = '1' or valids1(to_integer(unsigned(s_index))) = '1' then 
			if s_tag = tags0(to_integer(unsigned(s_index))) or s_tag = tags1(to_integer(unsigned(s_index))) then 
				data <= mainmem(to_integer(unsigned(s_offset))); 
				hit_addr <= '1'; 
				miss <= '0';
			end if; 
		else 
			hit_addr <= '0'; 
			if s_tag(0) = '0' then
				cache0(to_integer(unsigned(s_index)))(to_integer(unsigned(s_index))) <= s_tag;
				dirtys0(to_integer(unsigned(s_index))) <= '1'; 
				valids0(to_integer(unsigned(s_index))) <= '1';
				tags0(to_integer(unsigned(s_index))) <= s_tag;
			else
				cache1(to_integer(unsigned(s_index)))(to_integer(unsigned(s_index))) <= s_tag;
				dirtys1(to_integer(unsigned(s_index))) <= '1'; 
				valids1(to_integer(unsigned(s_index))) <= '1';
				tags1(to_integer(unsigned(s_index))) <= s_tag;
			end if; 
			miss <= '1'; 
			hit_addr <= '0'; 
			
		end if; 
		
	end if; 
end process;

	tag_out <= s_tag; 
	index_out <= s_index;
	offset_out <= s_offset;
	hit <= hit_addr; 
	data_out <= data;
	miss_out <= miss; 

END TypeArchitecture;

// VHDL entity cacheLRU, as the project stores it:
--------------------------------------------------------------------------------
-- Description :
-- Cache for pipelined MIPS processor. 
-- 2 way associative.
-- 32 bit addresses and 32 bit data output. 
-- Address is divided this way: 
--  tag is of 17 bits, index is of 8 bits and offset is 5 bits. 
--------------------------------------------------------------------------------

LIBRARY ieee;
USE ieee.std_logic_1164.all;

USE ieee.numeric_std.all;  

ENTITY cacheLRU IS
  PORT (
  ------------------------------------------------------------------------------
  -- Input ports
    clock      : IN  std_logic;           
    Address: IN std_logic_vector(31 DOWNTO 0);

  ------------------------------------------------------------------------------
  -- Output ports
	hit : OUT std_logic; 
	data_out: OUT std_logic_vector(31 DOWNTO 0);
		tag_out : OUT std_logic_vector (20 DOWNTO 0); 
		index_out : OUT std_logic_vector (4 DOWNTO 0); 
		offset_out :OUT std_logic_vector (5 DOWNTO 0);
	miss_out: OUT std_logic;
	set_0: OUT std_logic; 
	set_1: OUT std_logic
    );
END cacheLRU;

--------------------------------------------------------------------------------
-- Architecture of the cacheLRU entity
--------------------------------------------------------------------------------

ARCHITECTURE TypeArchitecture OF cacheLRU IS

-- Cache block definition: array of 64 blocks of 20-bit words
type bloque is array(0 to 63) of std_logic_vector(20 downto 0);

-- Cache set definition: array of 256 cache blocks
type t_set is array(0 to 255) of bloque;

-- Two sets for the 2-way associative cache
signal cache0 : t_set;
signal cache1 : t_set; 

-- Tag, valid, dirty, and LRU signal definitions
type t_tag is array(0 to 255) of std_logic_vector(20 downto 0);
type t_valid is array(0 to 255) of std_logic;
type t_Dirty is array(0 to 255) of std_logic;
type t_LRU is array(0 to 255) of std_logic; 

-- Internal signals for tag, index, offset, and data
signal s_tag : std_logic_vector(20 downto 0);
signal s_index :std_logic_vector (4 DOWNTO 0); 
signal s_offset : std_logic_vector (5 DOWNTO 0); 
signal data: std_logic_vector(31 DOWNTO 0); 
signal hit_addr : std_logic;

-- Main memory definition: array of 32 words of 32 bits
type t_Memory is array (0 to 31) of std_logic_vector(31 downto 0);
signal mainmem : t_Memory:= ("00000000000000000000000000000001",others =>"00000000000000000000000000100000");

-- Signals for dirty, valid, tag, and LRU bits for both cache sets
signal dirtys0 : t_Dirty:= ( others => '0');
signal valids0 : t_valid:= ( others => '0');
signal tags0 : t_tag:=( others => "000000000000000000000");
signal lru0: t_LRU:=(others => '0'); 

signal dirtys1 : t_Dirty:= ( others => '0');
signal valids1 : t_valid:= (others => '0');
signal tags1 : t_tag:=( others => "000000000000000000000");
signal lru1: t_LRU:=(others => '1'); 

-- Signal for miss logic
signal miss : std_logic; 

signal set_0_out: std_logic;
signal set_1_out : std_logic; 



BEGIN
-- Process that handles the cache behavior on clock edge
process (clock)
	begin
	if clock = '1' then
	-- Extracting tag, index, and offset from the address when clock is in its positive state 
		s_tag <= Address(31 DOWNTO 11); 
		s_index <= Address(10  DOWNTO 6); 
		s_offset <= Address(5  DOWNTO 0); 
		-- Default values for hit and miss signals 
		hit_addr <= '0'; 
		miss <= '1'; 

		-- Check if the address is in the cache (this is when valid bit and tag match) 
		if valids0(to_integer(unsigned(s_index))) = '1' or valids1(to_integer(unsigned(s_index))) = '1' then 
			if s_tag = tags0(to_integer(unsigned(s_index))) or s_tag = tags1(to_integer(unsigned(s_index))) then 
				-- If found, read data from main memory
				data <= mainmem(to_integer(unsigned(s_offset))); 
				hit_addr <= '1'; 
				miss <= '0';
			end if; 
		end if; 
		-- Determine which set to used based on LRU bit. Check if the tag is not stored already in the cache 
		if lru0(to_integer(unsigned(s_index))) = '0'and tags1(to_integer(unsigned(s_index))) /= s_tag  then 

				-- Use set 0 
				valids0(to_integer(unsigned(s_index))) <= '1';
				
				-- Actual lru_0 bit changes to '1' and the other lru_1 bit changes to '0' in the index from address.  
				lru0(to_integer(unsigned(s_index))) <= '1'; 
				lru1(to_integer(unsigned(s_index))) <= '0';
				
				-- Save tag in cache0
				cache0(to_integer(unsigned(s_index)))(to_integer(unsigned(s_offset))) <= s_tag;

				-- Add the tag to tags0 
				tags0(to_integer(unsigned(s_index))) <= s_tag;

		
				set_1_out <= '0'; 
				set_0_out <= '1';
		elsif lru1(to_integer(unsigned(s_index))) = '0' and tags0(to_integer(unsigned(s_index))) /= s_tag then 
				-- Use set 1 
				valids1(to_integer(unsigned(s_index))) <= '1';
				
				-- Actual lru_1 bit changes to '1' and the other lru_0 bit changes to '0' in the index from address.  
				lru1(to_integer(unsigned(s_index))) <= '1'; 
				lru0(to_integer(unsigned(s_index))) <= '0'; 
				-- Save tag in cache1
				cache1(to_integer(unsigned(s_index)))(to_integer(unsigned(s_offset))) <= s_tag;

				-- Add the tag to tags1
				tags1(to_integer(unsigned(s_index))) <= s_tag;


				set_1_out <= '1'; 
				set_0_out <= '0'; 
		end if;
	end if; 
end process;

	-- Assign internal signals to output ports 
	tag_out <= s_tag; 
	index_out <= s_index;
	offset_out <= s_offset;
	hit <= hit_addr; 
	data_out <= data;
	miss_out <= miss; 
	set_0 <= set_0_out; 
	set_1 <= set_1_out;

END TypeArchitecture;
