// Logisim project Multiprocesador.circ as structural Verilog: 1 circuit, main circuit Main
module Main (
);

  wire Encender_MIPS, Limpiar_RAM, MIPS_Escribir, MIPS_Solicitar_RAM, not_1_out, Poder, Reloj,
       Usar_Little_Endian;
  wire [7:0] RAM_Byte;
  wire [15:0] RAM_Nibble;
  wire [23:0] bit_extender_1_out;
  wire [29:0] four_gb_address_endian_translator_1_word;
  wire [31:0] MIPS_Direccion_RAM, MIPS_Entrada_RAM, MIPS_Indice_Instruccion, RAM_Word, ROM_Word;

  // DipSwitch #(.number(3)) Opciones: pin names not known; wires that end beside it: Limpiar_RAM, Usar_Little_Endian, Poder
  Button u_Encender_MIPS (.out(Encender_MIPS));
  Clock u_Reloj (.out(Reloj));
  Four_GB_Address_Endian_Translator four_gb_address_endian_translator_1 (
    .Direccion_Byte(MIPS_Indice_Instruccion), .Usar_Little_Endian(Usar_Little_Endian),
    .Word(four_gb_address_endian_translator_1_word));  // open: Byte, Nibble
  not not_1 (not_1_out, MIPS_Solicitar_RAM);
  ROM #(.addrWidth(24), .dataWidth(32)) rom_1 (.addr(bit_extender_1_out), .data(ROM_Word));
  Bit_Extender #(.in_width(30), .out_width(24), .\type ("zero")) bit_extender_1 (
    .in(four_gb_address_endian_translator_1_word), .out(bit_extender_1_out));
  // MIPS_Processor mips_processor_1: pin names not known; wires that end beside it: Reloj, Poder, Encender_MIPS, ROM_Word, RAM_Word, RAM_Nibble, RAM_Byte, MIPS_Indice_Instruccion, MIPS_Solicitar_RAM, MIPS_Escribir, MIPS_Direccion_RAM, MIPS_Entrada_RAM
  Four_GB_RAM_Controller four_gb_ram_controller_1 (
    .Reloj(Reloj), .Limpiar(Limpiar_RAM), .Bloquear(not_1_out), .Escribir(MIPS_Escribir),
    .Direccion_32_bits(MIPS_Direccion_RAM), .Usar_Litte_Endian(Usar_Little_Endian),
    .Entrada(MIPS_Entrada_RAM), .Word(RAM_Word), .Nibble(RAM_Nibble), .Byte(RAM_Byte));  // open: Doubleword

  // Notes on the sheet:
  //   Configuración
  //   Unidades de Memoria
  //   Procesadores
endmodule
